# Fritzing sketch TSC_PiHat_ILD_V1_5.3 (saved by Fritzing 0.9.3b)
circuit board: 6.8cm x 7cm
breadboards: 4

parts:
  DS_3231 = Adafruit DS3231 [part_number="Adafruit #3013"]
  R3 = Resistor [tolerance=±5% resistance=4.7k package=THT]
  R4 = Resistor [tolerance=±5% resistance=4.7k package=THT]
  BC547 = TRANSISTOR_NPN [package=to-92-ammo]
  BC547_2 = TRANSISTOR_NPN [package=to-92-ammo]
  J1 = double row female pin header, 40 pins [form="♀ (female)"]
  R1 = Resistor [tolerance=±5% resistance=470 package=THT]
  R2 = Resistor [tolerance=±5% resistance=1k package=THT]
  ILD74 = IC, DIP package, 8 pins [chip_label=IC]
  R5 = Resistor [tolerance=±5% resistance=220 package=THT]
  R6 = Resistor [tolerance=±5% resistance=220 package=THT]
  5_2+0_7V_-/+ = Screw terminal - 2 pins [package=THT]
  D1 = Rectifier Diode [part_number=1N4001 package="300 mil [THT]"]
  FTDI = Adafruit FTDI Friend [part_number="Adafruit #284"]
  ST4_COM/N/E/S/W = screw terminal, 5 pins
  Sig1/Sleeve/Sig2 = screw terminal, 3 pins
  Arduino_Mini_5V = Arduino Pro Mini v13
  SPI_Mo/Mi(5V)/Cl/SS1 = screw terminal, 4 pins
  -/TMP/+ = screw terminal, 3 pins
  GPS = screw terminal, 4 pins
  R10 = Resistor [tolerance=±5% resistance=118k package=THT]
  R7 = Resistor [tolerance=±5% resistance=118k package=THT]
  R9 = Resistor [tolerance=±5% resistance=118k package=THT]
  R8 = Resistor [tolerance=±5% resistance=118k package=THT]
  EStop = female pin header, 2 pins [form="♀ (female)"]

nets:
  N1: DS_3231.Vin, J1.pin1, EStop.pin2
  GND: DS_3231.GND, BC547.E, BC547_2.E, J1.pin5, R2.Pin_1, 5_2+0_7V_-/+.pin2, FTDI.GND, ST4_COM/N/E/S/W.pin5, Arduino_Mini_5V.GND, -/TMP/+.pin3, GPS.pin3
  N2: DS_3231.SCL, J1.pin3
  N3: DS_3231.SDA, J1.pin2
  N4: R3.Pin_0, J1.pin23
  N5: R3.Pin_1, BC547.B
  N6: R4.Pin_0, J1.pin35
  N7: R4.Pin_1, BC547_2.B
  N8: BC547.C, ILD74.pin3
  N9: BC547_2.C, ILD74.pin2
  N10: J1.pin10, Arduino_Mini_5V.D11_PWM/MOSI, SPI_Mo/Mi(5V)/Cl/SS1.pin1
  N11: J1.pin11, R1.Pin_1, R2.Pin_0
  N12: J1.pin12, Arduino_Mini_5V.D13/SCK, SPI_Mo/Mi(5V)/Cl/SS1.pin3
  N13: J1.pin28, SPI_Mo/Mi(5V)/Cl/SS1.pin4
  N14: J1.pin29, Arduino_Mini_5V.D10_PWM/SS
  N15: J1.pin33, EStop.pin1
  N16: J1.pin36, FTDI.TX
  N17: J1.pin37, FTDI.RX
  N18: J1.pin40, R5.Pin_0, R6.Pin_1, D1.cathode, FTDI.VCC, Arduino_Mini_5V.RAW, -/TMP/+.pin1, GPS.pin4, R10.Pin_0, R7.Pin_0, R9.Pin_0, R8.Pin_0
  N19: R1.Pin_0, Arduino_Mini_5V.D12/MISO, SPI_Mo/Mi(5V)/Cl/SS1.pin2
  N20: ILD74.pin1, R5.Pin_1
  N21: ILD74.pin4, R6.Pin_0
  N22: ILD74.pin5, ILD74.pin8, Sig1/Sleeve/Sig2.pin2
  N23: ILD74.pin6, Sig1/Sleeve/Sig2.pin3
  N24: ILD74.pin7, Sig1/Sleeve/Sig2.pin1
  N25: 5_2+0_7V_-/+.pin1, D1.anode
  N26: ST4_COM/N/E/S/W.pin1, Arduino_Mini_5V.A3, R10.Pin_1
  N27: ST4_COM/N/E/S/W.pin2, Arduino_Mini_5V.A2, R9.Pin_1
  N28: ST4_COM/N/E/S/W.pin3, Arduino_Mini_5V.A0, R8.Pin_1
  N29: ST4_COM/N/E/S/W.pin4, Arduino_Mini_5V.A1, R7.Pin_1
  N30: Arduino_Mini_5V.A4, -/TMP/+.pin2
  N31: Arduino_Mini_5V.D9_PWM, GPS.pin1
  N32: Arduino_Mini_5V.D8, GPS.pin2

notes:
  DSLR
  mount RTC with
  battery below
  Vin/GND/TX/RX
  TSC  V1.5.3
  W. Birkfellner 2019

custom parts:
  Adafruit DS3231: The datasheet for the DS3231 explains that this part is an "Extremely Accurate I²C-Integrated RTC/TCXO/Crystal". And, hey, it does exactly what it says on the tin! This Real Time Clock (RTC) is the most precise you can get in a small, low power package. Most RTCs use an external 32kHz timing crystal that is used to keep time with low current draw. And that's all well and good, but those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
  Adafruit FTDI Friend: Long gone are the days of parallel ports and serial ports. Now the USB port reigns supreme! But USB is hard, and you just want to transfer your every-day serial data from a microcontroller to computer. What now? Enter the FTDI Friend! The FTDI Friend is a tweaked out FTDI FT232RL chip adapter. Sure, like the well-known FTDI cable, it can provide power to your project and there are 4 signal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
