# Fritzing sketch AMIS30543_Teensy_2 (saved by Fritzing 0.9.3b)
circuit board: 9cm x 7.5cm
breadboards: 3

parts:
  GND/VMOT = female pin header, 2 pins [form="♀ (female)"]
  VD(Out)/IORef = female pin header, 2 pins [form="♀ (female)"]
  D1 = Rectifier Diode 10A [part_number=P1000K]
  AMIS_30543 = female pin header, 11 pins [form="♀ (female)"]
  - = female pin header, 1 pin [form="♀ (female)"]
  -_2 = female pin header, 1 pin [form="♀ (female)"]
  GND/+ = screw terminal, 2 pins
  Teensy_4 = Teensy 3.0
  AMIS_30544 = female pin header, 11 pins [form="♀ (female)"]
  VMOT/GND1 = female pin header, 2 pins [form="♀ (female)"]
  VD(Out)/IORef1 = female pin header, 2 pins [form="♀ (female)"]
  Teensy_4_2 = Teensy 3.0
  Fuse = Screw terminal - 2 pins [package=THT]
  AA'BB' = female pin header, 4 pins [form="♀ (female)"]
  AA'BB'_2 = female pin header, 4 pins [form="♀ (female)"]
  AA'BB'_3 = screw terminal, 4 pins
  AA'BB'_4 = screw terminal, 4 pins
  ST4 = RJ11 Jack [package=rj11-6]
  N/S/W = screw terminal, 3 pins
  E/COM = Screw terminal - 2 pins [package=THT]

nets:
  N1: GND/VMOT.pin1, GND/+.pin1, VMOT/GND1.pin1
  N2: GND/VMOT.pin2, VMOT/GND1.pin2, Fuse.pin2
  N3: VD(Out)/IORef.pin1, Teensy_4.3V3
  N4: D1.cathode, -.pin1, Fuse.pin1
  N5: D1.anode, -_2.pin1, GND/+.pin2
  N6: AMIS_30543.pin3, Teensy_4.D3
  N7: AMIS_30543.pin4, Teensy_4.D0
  N8: AMIS_30543.pin5, Teensy_4.D10
  N9: AMIS_30543.pin6, Teensy_4.D13
  N10: AMIS_30543.pin7, Teensy_4.D11
  N11: AMIS_30543.pin8, Teensy_4.D12
  N12: AMIS_30543.pin9, Teensy_4.D2
  N13: AMIS_30543.pin10, Teensy_4.D1
  N14: AMIS_30543.pin11, Teensy_4.GND
  N15: AMIS_30544.pin3, Teensy_4_2.D3
  N16: AMIS_30544.pin4, Teensy_4_2.D0
  N17: AMIS_30544.pin5, Teensy_4_2.D10
  N18: AMIS_30544.pin6, Teensy_4_2.D13
  N19: AMIS_30544.pin7, Teensy_4_2.D11
  N20: AMIS_30544.pin8, Teensy_4_2.D12
  N21: AMIS_30544.pin9, Teensy_4_2.D2
  N22: AMIS_30544.pin10, Teensy_4_2.D1
  N23: AMIS_30544.pin11, Teensy_4_2.GND
  N24: VD(Out)/IORef1.pin1, Teensy_4_2.3V3
  N25: AA'BB'.pin1, AA'BB'_3.pin4
  N26: AA'BB'.pin2, AA'BB'_3.pin3
  N27: AA'BB'.pin3, AA'BB'_3.pin2
  N28: AA'BB'.pin4, AA'BB'_3.pin1
  N29: AA'BB'_2.pin1, AA'BB'_4.pin4
  N30: AA'BB'_2.pin2, AA'BB'_4.pin3
  N31: AA'BB'_2.pin3, AA'BB'_4.pin2
  N32: AA'BB'_2.pin4, AA'BB'_4.pin1
  N33: ST4.1, N/S/W.pin1
  N34: ST4.2, N/S/W.pin2
  N35: ST4.3, N/S/W.pin3
  N36: ST4.4, E/COM.pin2
  N37: ST4.5, E/COM.pin1

notes:
  GND
  NXT/STEP
  DIR
  DO
  DI
  CLK
  CS
  CLR
  SLA
  POR/WD
  ERR
