# Fritzing sketch AMIS30543_Teensy_4 (saved by Fritzing 0.9.10b)
circuit board: 8.5cm x 7cm
breadboards: 4

parts:
  GND/VMOT = female pin header, 2 pins [form="♀ (female)"]
  VD(Out)/IORef = female pin header, 2 pins [form="♀ (female)"]
  AMIS_30543 = female pin header, 11 pins [form="♀ (female)"]
  GND/+ = screw terminal, 2 pins
  Teensy_4 = Teensy 3.0
  AMIS_30544 = female pin header, 11 pins [form="♀ (female)"]
  VMOT/GND1 = female pin header, 2 pins [form="♀ (female)"]
  VD(Out)/IORef1 = female pin header, 2 pins [form="♀ (female)"]
  Teensy_4_2 = Teensy 3.0
  AA'BB' = female pin header, 4 pins [form="♀ (female)"]  # not connected
  AA'BB'_2 = female pin header, 4 pins [form="♀ (female)"]  # not connected
  S/N/E = screw terminal, 3 pins
  COM/W = Screw terminal - 2 pins [package=THT]
  ST4 = RJ11 Jack [package=rj11-6]
  Fuse = Screw terminal - 2 pins [package=THT]
  D1 = Rectifier Diode 10A [part_number=P1000K]
  part = female pin header, 1 pin [form="♀ (female)"]
  part_2 = female pin header, 1 pin [form="♀ (female)"]
  GPS_Rx/Tx/GND/Vin = screw terminal, 4 pins
  GPS_Friend = Adafruit Ultimate GPS v3 [part_number="Adafruit #746"]

nets:
  N1: GND/VMOT.pin1, GND/+.pin1, VMOT/GND1.pin1
  N2: GND/VMOT.pin2, VMOT/GND1.pin2, Fuse.pin2
  N3: VD(Out)/IORef.pin1, Teensy_4.3V3
  N4: AMIS_30543.pin3, Teensy_4.D3
  N5: AMIS_30543.pin4, Teensy_4.D0
  N6: AMIS_30543.pin5, Teensy_4.D10
  N7: AMIS_30543.pin6, Teensy_4.D13
  N8: AMIS_30543.pin7, Teensy_4.D11
  N9: AMIS_30543.pin8, Teensy_4.D12
  N10: AMIS_30543.pin9, Teensy_4.D2
  N11: AMIS_30543.pin10, Teensy_4.D1
  N12: AMIS_30543.pin11, Teensy_4.GND
  N13: GND/+.pin2, D1.anode, part.pin1
  N14: AMIS_30544.pin3, Teensy_4_2.D3
  N15: AMIS_30544.pin4, Teensy_4_2.D0
  N16: AMIS_30544.pin5, Teensy_4_2.D10
  N17: AMIS_30544.pin6, Teensy_4_2.D13
  N18: AMIS_30544.pin7, Teensy_4_2.D11
  N19: AMIS_30544.pin8, Teensy_4_2.D12
  N20: AMIS_30544.pin9, Teensy_4_2.D2
  N21: AMIS_30544.pin10, Teensy_4_2.D1
  N22: AMIS_30544.pin11, Teensy_4_2.GND
  N23: VD(Out)/IORef1.pin1, Teensy_4_2.3V3
  N24: S/N/E.pin1, ST4.6
  N25: S/N/E.pin2, ST4.5
  N26: S/N/E.pin3, ST4.4
  N27: COM/W.pin1, ST4.3
  N28: COM/W.pin2, ST4.2
  N29: Fuse.pin1, D1.cathode, part_2.pin1
  N30: GPS_Rx/Tx/GND/Vin.pin1, GPS_Friend.3.3V
  N31: GPS_Rx/Tx/GND/Vin.pin2, GPS_Friend.GND
  N32: GPS_Rx/Tx/GND/Vin.pin3, GPS_Friend.TX
  N33: GPS_Rx/Tx/GND/Vin.pin4, GPS_Friend.RX

notes:
  TSC Driver V. 3

custom parts:
  Adafruit Ultimate GPS v3: We carry a few different GPS modules here in the Adafruit shop, but none that satisfied our every desire - that's why we designed this little GPS breakout board. We believe this is the Ultimate GPS module, so we named it that. It's got everything you want and more: -165 dBm sensitivity, 10 Hz updates, 66 channels 5V friendly design and only 20mA current draw Breadboard friendly + two mounting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
