# Fritzing sketch TCP_Handbox (saved by Fritzing 0.9.3b)
circuit board: 7cm x 7cm
breadboards: 2

parts:
  3_3V/GND/SCL/SDA = screw terminal, 4 pins
  R8 = Resistor [tolerance=±5% resistance=10k package=THT]
  R10 = Resistor [tolerance=±5% resistance=10k package=THT]
  R5 = Resistor [tolerance=±5% resistance=10k package=THT]
  R6 = Resistor [tolerance=±5% resistance=10k package=THT]
  R7 = Resistor [tolerance=±5% resistance=10k package=THT]
  R4 = Resistor [tolerance=±5% resistance=10k package=THT]
  R3 = Resistor [tolerance=±5% resistance=10k package=THT]
  R2 = Resistor [tolerance=±5% resistance=10k package=THT]
  R1 = Resistor [tolerance=±5% resistance=10k package=THT]
  R9 = Resistor [tolerance=±5% resistance=10k package=THT]
  Full = SWITCH-MOMENTARY-2 [package=tactile-pth]
  F/5 = SWITCH-MOMENTARY-2 [package=tactile-pth]
  F/20 = SWITCH-MOMENTARY-2 [package=tactile-pth]
  N = SWITCH-MOMENTARY-2 [package=tactile-pth-12mm]
  W = SWITCH-MOMENTARY-2 [package=tactile-pth-12mm]
  E = SWITCH-MOMENTARY-2 [package=tactile-pth-12mm]
  S = SWITCH-MOMENTARY-2 [package=tactile-pth-12mm]
  S1 = female pin header, 3 pins [form="♀ (female)"]
  S2 = female pin header, 3 pins [form="♀ (female)"]
  S3 = female pin header, 3 pins [form="♀ (female)"]
  WEMOS_Lolin_D32_Pro = Wemos Lolin32lite
  BAT_+/GND = Screw terminal - 2 pins [package=THT]
  D1 = Rectifier Diode [part_number=1N4001 package="300 mil [THT]"]

nets:
  N1: 3_3V/GND/SCL/SDA.pin1, Full.1, F/5.1, F/20.1, N.1, W.1, E.1, S.1, S1.pin2, S2.pin2, S3.pin2, WEMOS_Lolin_D32_Pro.pin_1
  N2: 3_3V/GND/SCL/SDA.pin2, R8.Pin_0, R10.Pin_0, R5.Pin_0, R6.Pin_0, R7.Pin_0, R4.Pin_0, R3.Pin_0, R2.Pin_0, R1.Pin_0, R9.Pin_0, WEMOS_Lolin_D32_Pro.pin_15, WEMOS_Lolin_D32_Pro.pin_21, WEMOS_Lolin_D32_Pro.pin_34
  N3: 3_3V/GND/SCL/SDA.pin3, WEMOS_Lolin_D32_Pro.pin_32
  N4: 3_3V/GND/SCL/SDA.pin4, WEMOS_Lolin_D32_Pro.pin_29
  N5: R8.Pin_1, S3.pin1, WEMOS_Lolin_D32_Pro.pin_10
  N6: R10.Pin_1, S1.pin1, WEMOS_Lolin_D32_Pro.pin_8
  N7: R5.Pin_1, F/20.2, WEMOS_Lolin_D32_Pro.pin_20
  N8: R6.Pin_1, F/5.2, WEMOS_Lolin_D32_Pro.pin_26
  N9: R7.Pin_1, Full.2, WEMOS_Lolin_D32_Pro.pin_22
  N10: R4.Pin_1, W.2, WEMOS_Lolin_D32_Pro.pin_23
  N11: R3.Pin_1, S.2, WEMOS_Lolin_D32_Pro.pin_13
  N12: R2.Pin_1, E.2, WEMOS_Lolin_D32_Pro.pin_12
  N13: R1.Pin_1, N.2, WEMOS_Lolin_D32_Pro.pin_11
  N14: R9.Pin_1, S2.pin1, WEMOS_Lolin_D32_Pro.pin_9
  N15: WEMOS_Lolin_D32_Pro.pin_16, D1.cathode
  N16: WEMOS_Lolin_D32_Pro.pin_19, BAT_+/GND.pin1
  N17: BAT_+/GND.pin2, D1.anode

notes:
  I2C OLED
  TSC TCP/IP Handbox V. 1.1
  W. Birkfellner 2019
  Pins are different!

custom parts:
  Wemos Lolin32lite: Wemos Lolin32 pro wifi and blue tooth board based on the ESP-32 cpu, digital I/Os 22, analog inputs 6, analog outputs 2, clock 240mhz, Flash 4Mbytes, PSRAM 4MB, microSD card slot, lipo battery charger (500ma connection broken out on breadboard but not pcb), usb.
