# Fritzing sketch MotorBoard (saved by Fritzing 0.9.3b)
circuit board: 5.43583cm x 6.97882cm
breadboards: 1

parts:
  Arduino_Mini_Pro = Arduino Pro Mini v13
  Drive_B = female pin header, 8 pins [form="♀ (female)"]
  EN = female pin header, 8 pins [form="♀ (female)"]
  Drive_A = female pin header, 8 pins [form="♀ (female)"]
  EN_2 = female pin header, 8 pins [form="♀ (female)"]
  GND/12V = Screw terminal - 2 pins [package=THT]
  D1 = Rectifier Diode [part_number=1N4001 package="300 mil [THT]"]
  DR_B_AA'BB' = screw terminal, 4 pins
  DR_A_AA'BB' = screw terminal, 4 pins
  SPI = screw terminal, 4 pins
  GND/5V = Screw terminal - 2 pins [package=THT]
  C1 = Electrolytic Capacitor [capacitance=0.1mF voltage=20V package="100 mil [THT, electrolytic]"]
  D2 = P1000K [part_number=P1000K]

nets:
  N1: Arduino_Mini_Pro.RAW, Drive_B.pin7, Drive_A.pin7, D1.cathode
  N2: Arduino_Mini_Pro.GND, Drive_B.pin8, Drive_A.pin8, GND/5V.pin1
  N3: Arduino_Mini_Pro.A1, EN.pin1
  N4: Arduino_Mini_Pro.A0, EN_2.pin1
  N5: Arduino_Mini_Pro.D13/SCK, SPI.pin2
  N6: Arduino_Mini_Pro.D12/MISO, SPI.pin3
  N7: Arduino_Mini_Pro.D11_PWM/MOSI, SPI.pin4
  N8: Arduino_Mini_Pro.D10_PWM/SS, SPI.pin1
  N9: Arduino_Mini_Pro.D8, EN.pin2, EN_2.pin2
  N10: Arduino_Mini_Pro.D7, EN.pin3, EN_2.pin3
  N11: Arduino_Mini_Pro.D6_PWM, EN.pin4, EN_2.pin4
  N12: Arduino_Mini_Pro.D5_PWM, EN.pin7
  N13: Arduino_Mini_Pro.D4, EN.pin8
  N14: Arduino_Mini_Pro.D3_PWM, EN_2.pin7
  N15: Arduino_Mini_Pro.D2, EN_2.pin8
  N16: Drive_B.pin1, Drive_A.pin1, C1.+, D2.cathode
  N17: Drive_B.pin2, Drive_A.pin2, GND/12V.pin1, C1.-
  N18: Drive_B.pin3, DR_B_AA'BB'.pin4
  N19: Drive_B.pin4, DR_B_AA'BB'.pin3
  N20: Drive_B.pin5, DR_B_AA'BB'.pin2
  N21: Drive_B.pin6, DR_B_AA'BB'.pin1
  N22: EN.pin5, EN.pin6
  N23: Drive_A.pin3, DR_A_AA'BB'.pin1
  N24: Drive_A.pin4, DR_A_AA'BB'.pin2
  N25: Drive_A.pin5, DR_A_AA'BB'.pin3
  N26: Drive_A.pin6, DR_A_AA'BB'.pin4
  N27: EN_2.pin5, EN_2.pin6
  N28: GND/12V.pin2, D2.anode
  N29: D1.anode, GND/5V.pin2

notes:
  SS/SCK/MISO/MOSI
  TSC
  Focusdrive
  W. Birkfellner
  2019-V1.11
