# Fritzing sketch AMIS30543 (saved by Fritzing 0.9.3b)
circuit board: 5.71179cm x 4.49412cm
breadboards: 2

parts:
  VMOT/GND = female pin header, 2 pins [form="♀ (female)"]
  VD(Out)/IORef = female pin header, 2 pins [form="♀ (female)"]
  MXP/MXN/MYN/MYP = female pin header, 4 pins [form="♀ (female)"]
  ItsyBitsy_M4 = Adafruit ItsyBitsy M4 [part_number="Adafruit #3800"]
  D1 = Rectifier Diode 10A [part_number=P1000K]
  AMIS_30543 = female pin header, 11 pins [form="♀ (female)"]
  part = female pin header, 1 pin [form="♀ (female)"]
  part_2 = female pin header, 1 pin [form="♀ (female)"]
  C1 = Electrolytic Capacitor [capacitance=4.7mF voltage=63V package="200 mil [THT, electrolytic]"]
  C2 = Ceramic Capacitor [capacitance=100nF voltage=63V package="100 mil [THT, multilayer]"]
  AA'_BB' = screw terminal, 4 pins
  V+/GND = screw terminal, 2 pins
  IO-Pins = screw terminal, 3 pins

nets:
  N1: VMOT/GND.pin1, D1.cathode, part.pin1, C1.+, C2.1
  N2: VMOT/GND.pin2, ItsyBitsy_M4.GND, AMIS_30543.pin11, C1.-, C2.0, V+/GND.pin1, IO-Pins.pin3
  N3: VD(Out)/IORef.pin1, ItsyBitsy_M4.VHI
  N4: MXP/MXN/MYN/MYP.pin1, AA'_BB'.pin4
  N5: MXP/MXN/MYN/MYP.pin2, AA'_BB'.pin3
  N6: MXP/MXN/MYN/MYP.pin3, AA'_BB'.pin2
  N7: MXP/MXN/MYN/MYP.pin4, AA'_BB'.pin1
  N8: ItsyBitsy_M4.D3, IO-Pins.pin2
  N9: ItsyBitsy_M4.D4, IO-Pins.pin1
  N10: ItsyBitsy_M4.D12, AMIS_30543.pin10
  N11: ItsyBitsy_M4.D11, AMIS_30543.pin3
  N12: ItsyBitsy_M4.D10, AMIS_30543.pin4
  N13: ItsyBitsy_M4.D9, AMIS_30543.pin5
  N14: ItsyBitsy_M4.D7, AMIS_30543.pin9
  N15: ItsyBitsy_M4.MISO, AMIS_30543.pin8
  N16: ItsyBitsy_M4.MOSI, AMIS_30543.pin7
  N17: ItsyBitsy_M4.SCK, AMIS_30543.pin6
  N18: D1.anode, part_2.pin1, V+/GND.pin2

notes:
  GND
  NXT/STEP
  DIR
  DO
  DI
  CLK
  CS
  CLR
  ERR
  POR/WD
  SLA
  USB
  Stepper Driver Board V. 1.2
  W. Birkfellner 2018

custom parts:
  Adafruit ItsyBitsy M4: What's smaller than a Feather but larger than a Trinket? It's an Adafruit ItsyBitsy M4 Express featuring the Microchip ATSAMD51! Small, powerful, with a ultra fast ATSAMD51 Cortex M4 processor running at 120 MHz - this microcontroller board is perfect when you want something very compact, with a ton of horsepower and a bunch of pins. This Itsy is like a bullet train, with it's 120MHz Cortex M4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
