# Fritzing sketch AMIS30543_Teensy (saved by Fritzing 0.9.3b)
circuit board: 5cm x 6.28241cm
breadboards: 2

parts:
  VMOT/GND = female pin header, 2 pins [form="♀ (female)"]
  VD(Out)/IORef = female pin header, 2 pins [form="♀ (female)"]
  D1 = Rectifier Diode 10A [part_number=P1000K]
  AMIS_30543 = female pin header, 11 pins [form="♀ (female)"]
  part = female pin header, 1 pin [form="♀ (female)"]
  part_2 = female pin header, 1 pin [form="♀ (female)"]
  +/GND_Drive = screw terminal, 2 pins
  Fuse = Screw terminal - 2 pins [package=THT]
  part_3 = female pin header, 24 pins [form="♀ (female)"]
  part_4 = female pin header, 24 pins [form="♀ (female)"]

nets:
  N1: VMOT/GND.pin1, Fuse.pin2
  N2: VMOT/GND.pin2, +/GND_Drive.pin1
  N3: VD(Out)/IORef.pin1, part_4.pin15
  N4: D1.cathode, part.pin1, Fuse.pin1
  N5: D1.anode, part_2.pin1, +/GND_Drive.pin2
  N6: AMIS_30543.pin3, part_4.pin20
  N7: AMIS_30543.pin4, part_4.pin19
  N8: AMIS_30543.pin5, part_4.pin12
  N9: AMIS_30543.pin6, part_3.pin14
  N10: AMIS_30543.pin7, part_4.pin13
  N11: AMIS_30543.pin8, part_4.pin14
  N12: AMIS_30543.pin9, part_4.pin16
  N13: AMIS_30543.pin10, part_4.pin17
  N14: AMIS_30543.pin11, part_3.pin15

notes:
  GND
  NXT/STEP
  DIR
  DO
  DI
  CLK
  CS
  CLR
  ERR
  POR/WD
  SLA
  USB
  Stepper Driver Board V. 1
  W. Birkfellner 2019
