# Fritzing sketch AMIS30543_Teensy_1_3 (saved by Fritzing 0.9.3b)
circuit board: 5.12244cm x 6.28241cm
breadboards: 2

parts:
  VMOT/GND = female pin header, 2 pins [form="♀ (female)"]
  VD(Out)/IORef = female pin header, 2 pins [form="♀ (female)"]
  D1 = Rectifier Diode 10A [part_number=P1000K]
  AMIS_30543 = female pin header, 11 pins [form="♀ (female)"]
  J1 = female pin header, 1 pin [form="♀ (female)"]
  J2 = female pin header, 1 pin [form="♀ (female)"]
  GND/+ = screw terminal, 2 pins
  Fuse = Screw terminal - 2 pins [package=THT]
  J3 = female pin header, 24 pins [form="♀ (female)"]
  J4 = female pin header, 24 pins [form="♀ (female)"]

nets:
  N1: VMOT/GND.pin1, GND/+.pin1
  N2: VMOT/GND.pin2, Fuse.pin2
  N3: VD(Out)/IORef.pin1, J4.pin15
  N4: D1.cathode, J1.pin1, Fuse.pin1
  N5: D1.anode, J2.pin1, GND/+.pin2
  N6: AMIS_30543.pin3, J4.pin20
  N7: AMIS_30543.pin4, J4.pin19
  N8: AMIS_30543.pin5, J4.pin12
  N9: AMIS_30543.pin6, J3.pin14
  N10: AMIS_30543.pin7, J4.pin13
  N11: AMIS_30543.pin8, J4.pin14
  N12: AMIS_30543.pin9, J4.pin16
  N13: AMIS_30543.pin10, J4.pin17
  N14: AMIS_30543.pin11, J3.pin15

notes:
  GND
  NXT/STEP
  DIR
  DO
  DI
  CLK
  CS
  CLR
  ERR
  POR/WD
  SLA
  USB
  Stepper Driver Board V. 1.3
  W. Birkfellner 2019
