# Fritzing sketch AMIS30543_Teensy_1_3 (saved by Fritzing 0.9.3b)
circuit board: 5.12244cm x 6.28241cm
breadboards: 3

parts:
  VMOT/GND = female pin header, 2 pins [form="♀ (female)"]
  VD(Out)/IORef = female pin header, 2 pins [form="♀ (female)"]
  D1 = Rectifier Diode 10A [part_number=P1000K]
  AMIS_30543 = female pin header, 11 pins [form="♀ (female)"]
  J1 = female pin header, 1 pin [form="♀ (female)"]
  J2 = female pin header, 1 pin [form="♀ (female)"]
  GND/+ = screw terminal, 2 pins
  Fuse = Screw terminal - 2 pins [package=THT]
  Teensy_3_1 = Teensy 3.0
  AMIS_30544 = female pin header, 11 pins [form="♀ (female)"]
  VMOT/GND1 = female pin header, 2 pins [form="♀ (female)"]
  VD(Out)/IORef1 = female pin header, 2 pins [form="♀ (female)"]
  Teensy_3_2 = Teensy 3.0

nets:
  N1: VMOT/GND.pin1, GND/+.pin1, VMOT/GND1.pin1
  N2: VMOT/GND.pin2, Fuse.pin2, VMOT/GND1.pin2
  N3: VD(Out)/IORef.pin1, Teensy_3_1.3V3
  N4: D1.cathode, J1.pin1, Fuse.pin1
  N5: D1.anode, J2.pin1, GND/+.pin2
  N6: AMIS_30543.pin3, Teensy_3_1.D3
  N7: AMIS_30543.pin4, Teensy_3_1.D0
  N8: AMIS_30543.pin5, Teensy_3_1.D10
  N9: AMIS_30543.pin6, Teensy_3_1.D13
  N10: AMIS_30543.pin7, Teensy_3_1.D11
  N11: AMIS_30543.pin8, Teensy_3_1.D12
  N12: AMIS_30543.pin9, Teensy_3_1.D2
  N13: AMIS_30543.pin10, Teensy_3_1.D1
  N14: AMIS_30543.pin11, Teensy_3_1.GND
  N15: AMIS_30544.pin3, Teensy_3_2.D3
  N16: AMIS_30544.pin4, Teensy_3_2.D0
  N17: AMIS_30544.pin5, Teensy_3_2.D10
  N18: AMIS_30544.pin6, Teensy_3_2.D13
  N19: AMIS_30544.pin7, Teensy_3_2.D11
  N20: AMIS_30544.pin8, Teensy_3_2.D12
  N21: AMIS_30544.pin9, Teensy_3_2.D2
  N22: AMIS_30544.pin10, Teensy_3_2.D1
  N23: AMIS_30544.pin11, Teensy_3_2.GND
  N24: VD(Out)/IORef1.pin1, Teensy_3_2.3V3

notes:
  GND
  NXT/STEP
  DIR
  DO
  DI
  CLK
  CS
  CLR
  ERR
  POR/WD
  SLA
  USB
  Stepper Driver Board V. 1.3
  W. Birkfellner 2019
