# Fritzing sketch Bigger4DriveBoardV1.1 (saved by Fritzing 0.9.3b)
circuit board: 9cm x 8cm
breadboards: 4

parts:
  Aux_Drive_1_AA'BB' = screw terminal, 4 pins
  Main_Drive_2_AA'BB' = screw terminal, 4 pins
  Aux_Drive_2_AA'BB' = screw terminal, 4 pins
  C3 = Electrolytic Capacitor [capacitance=0.1mF voltage=63 package="200 mil [THT, electrolytic]"]
  C2 = Electrolytic Capacitor [capacitance=0.1mF voltage=63 package="200 mil [THT, electrolytic]"]
  Main_Drive_1_AA'BB' = screw terminal, 4 pins
  Main1 = Pololu A4988 [package=SO16]
  Main2 = Pololu A4988 [package=SO16]
  Aux1 = Pololu A4988 [package=SO16]
  Aux2 = Pololu A4988 [package=SO16]
  12V_+/- = Screw terminal - 2 pins [package=THT]
  5V_+/- = Screw terminal - 2 pins [package=THT]
  12V_+/-_2 = Screw terminal - 2 pins [package=THT]
  12V_-/+ = Screw terminal - 2 pins [package=THT]
  12V_-/+_2 = Screw terminal - 2 pins [package=THT]
  D4 = Rectifier Diode [part_number=1N4001 package="300 mil [THT]"]
  D3 = Rectifier Diode [part_number=1N4001 package="300 mil [THT]"]
  D2 = Rectifier Diode [part_number=1N4001 package="300 mil [THT]"]
  C4 = Electrolytic Capacitor [capacitance=0.1mF voltage=63 package="200 mil [THT, electrolytic]"]
  D1 = Rectifier Diode [part_number=1N4001 package="300 mil [THT]"]
  C1 = Electrolytic Capacitor [capacitance=0.1mF voltage=63 package="200 mil [THT, electrolytic]"]
  Teensy_GND = female pin header, 24 pins [form="♀ (female)"]
  Vin = female pin header, 24 pins [form="♀ (female)"]
  D5 = Rectifier Diode [part_number=1N4001 package="300 mil [THT]"]

nets:
  N1: Aux_Drive_1_AA'BB'.pin1, Aux1.2B
  N2: Aux_Drive_1_AA'BB'.pin2, Aux1.2A
  N3: Aux_Drive_1_AA'BB'.pin3, Aux1.1A
  N4: Aux_Drive_1_AA'BB'.pin4, Aux1.1B
  N5: Main_Drive_2_AA'BB'.pin1, Main2.2B
  N6: Main_Drive_2_AA'BB'.pin2, Main2.2A
  N7: Main_Drive_2_AA'BB'.pin3, Main2.1A
  N8: Main_Drive_2_AA'BB'.pin4, Main2.1B
  N9: Aux_Drive_2_AA'BB'.pin1, Aux2.2B
  N10: Aux_Drive_2_AA'BB'.pin2, Aux2.2A
  N11: Aux_Drive_2_AA'BB'.pin3, Aux2.1A
  N12: Aux_Drive_2_AA'BB'.pin4, Aux2.1B
  N13: C3.-, Aux1.GND#14, 12V_+/-_2.pin2
  N14: C3.+, Aux1.VMOT, D3.cathode
  N15: C2.-, Main2.GND#14, 12V_-/+.pin2
  N16: C2.+, Main2.VMOT, D2.cathode
  N17: Main_Drive_1_AA'BB'.pin1, Main1.2B
  N18: Main_Drive_1_AA'BB'.pin2, Main1.2A
  N19: Main_Drive_1_AA'BB'.pin3, Main1.1A
  N20: Main_Drive_1_AA'BB'.pin4, Main1.1B
  N21: Main1.ENABLE, Vin.pin18
  N22: Main1.MS1, Main2.MS1, Vin.pin13
  N23: Main1.MS2, Main2.MS2, Vin.pin14
  N24: Main1.MS3, Main2.MS3, Vin.pin15
  N25: Main1.RESET, Main1.SLEEP
  N26: Main1.STEP, Vin.pin19
  N27: Main1.DIR, Vin.pin20
  N28: Main1.GND#8, Main2.GND#8, Aux1.GND#8, Aux2.GND#8, 5V_+/-.pin2
  VDD: Main1.VDD, Main2.VDD, Aux1.VDD, Aux2.VDD, D5.cathode
  N29: Main1.GND#14, 12V_-/+_2.pin2, C1.-
  N30: Main1.VMOT, D1.cathode, C1.+
  N31: Main2.ENABLE, Vin.pin12
  N32: Main2.RESET, Main2.SLEEP
  N33: Main2.STEP, Vin.pin16
  N34: Main2.DIR, Vin.pin17
  N35: Aux1.ENABLE, Vin.pin1
  N36: Aux1.MS1, Aux2.MS1, Vin.pin2
  N37: Aux1.MS2, Aux2.MS2, Vin.pin3
  N38: Aux1.MS3, Aux2.MS3, Vin.pin4
  N39: Aux1.RESET, Aux1.SLEEP
  N40: Aux1.STEP, Vin.pin5
  N41: Aux1.DIR, Vin.pin6
  N42: Aux2.ENABLE, Vin.pin7
  N43: Aux2.RESET, Aux2.SLEEP
  N44: Aux2.STEP, Teensy_GND.pin1
  N45: Aux2.DIR, Teensy_GND.pin2
  N46: Aux2.GND#14, 12V_+/-.pin2, C4.-
  N47: Aux2.VMOT, D4.cathode, C4.+
  N48: 12V_+/-.pin1, D4.anode
  N49: 5V_+/-.pin1, D5.anode
  N50: 12V_+/-_2.pin1, D3.anode
  N51: 12V_-/+.pin1, D2.anode
  N52: 12V_-/+_2.pin1, D1.anode
