# Fritzing sketch Handbox (saved by Fritzing 0.9.0b)
circuit board: 7.68277cm x 4.98953cm
breadboards: 1

parts:
  S1 = Momentary Switch [package=ksa_sealed_tac_switch]
  R1 = Resistor [tolerance=±5% resistance=10k package=THT]
  S2 = Momentary Switch [package=ksa_sealed_tac_switch]
  S4 = Momentary Switch [package=ksa_sealed_tac_switch]
  R2 = Resistor [tolerance=±5% resistance=10k package=THT]
  R3 = Resistor [tolerance=±5% resistance=10k package=THT]
  R4 = Resistor [tolerance=±5% resistance=10k package=THT]
  R5 = Resistor [tolerance=±5% resistance=10k package=THT]
  05 = female pin header, 2 pins [form="♀ (female)"]
  HC = female pin header, 2 pins [form="♀ (female)"]
  VCC = female pin header, 2 pins [form="♀ (female)"]
  S3 = Momentary Switch [package=ksa_sealed_tac_switch]
  S_5 = female pin header, 2 pins [form="♀ (female)"]
  5_V = female pin header, 2 pins [form="♀ (female)"]
  Mini_Pro = Arduino Pro Mini v13
  D1 = Rectifier Diode [part_number=1N4001 package="300 mil [THT]"]

nets:
  N1: S1.1, Mini_Pro.D2
  N2: S1.2, R1.Pin_0
  N3: S1.4, S2.4, S4.4, VCC.pin2, S3.4, S_5.pin1, Mini_Pro.VCC
  N4: R1.Pin_1, R2.Pin_1, R3.Pin_1, R4.Pin_1, R5.Pin_1, 05.pin1, 5_V.pin1, Mini_Pro.GND
  N5: S2.1, Mini_Pro.D3_PWM
  N6: S2.2, R2.Pin_0
  N7: S4.1, Mini_Pro.D5_PWM
  N8: S4.2, R4.Pin_0
  N9: R3.Pin_0, S3.2
  N10: R5.Pin_0, S_5.pin2, Mini_Pro.D6_PWM
  N11: 05.pin2, Mini_Pro.D7
  N12: HC.pin1, Mini_Pro.D8
  N13: S3.1, Mini_Pro.D4
  N14: 5_V.pin2, D1.anode
  N15: Mini_Pro.RAW, D1.cathode

notes:
  TSC Handbox - W. Birkfellner 2017, V . 1.1
  +
  -
