# Fritzing sketch HandboxV1_2 (saved by Fritzing 0.9.3b)
circuit board: 7.5cm x 5cm
breadboards: 1

parts:
  4_5V_+/- = Screw terminal - 2 pins [package=THT]
  D1 = Rectifier Diode [part_number=1N4001 package="300 mil [THT]"]
  Switch_connectors = screw terminal, 12 pins
  R1 = Resistor [tolerance=±5% resistance=10k package=THT]
  R2 = Resistor [tolerance=±5% resistance=10k package=THT]
  R3 = Resistor [tolerance=±5% resistance=10k package=THT]
  R4 = Resistor [tolerance=±5% resistance=10k package=THT]
  R5 = Resistor [tolerance=±5% resistance=10k package=THT]
  R6 = Resistor [tolerance=±5% resistance=10k package=THT]
  R7 = Resistor [tolerance=±5% resistance=10k package=THT]
  R8 = Resistor [tolerance=±5% resistance=10k package=THT]
  R9 = Resistor [tolerance=±5% resistance=10k package=THT]
  R10 = Resistor [tolerance=±5% resistance=10k package=THT]
  Arduino_3_3V = Arduino Pro Mini v13
  S2 = SWITCH-MOMENTARY-2 [package=tactile-pth-12mm]
  S1 = SWITCH-MOMENTARY-2 [package=tactile-pth-12mm]
  S3 = SWITCH-MOMENTARY-2 [package=tactile-pth-12mm]
  S4 = SWITCH-MOMENTARY-2 [package=tactile-pth-12mm]
  HC_05 = screw terminal, 4 pins

nets:
  N1: 4_5V_+/-.pin1, R1.Pin_0, R2.Pin_0, R3.Pin_0, R4.Pin_0, R5.Pin_0, R6.Pin_0, R7.Pin_0, R8.Pin_0, R9.Pin_0, R10.Pin_0, Arduino_3_3V.GND, HC_05.pin2
  N2: 4_5V_+/-.pin2, D1.anode
  N3: D1.cathode, Arduino_3_3V.RAW, HC_05.pin1
  N4: Switch_connectors.pin1, Switch_connectors.pin3, Switch_connectors.pin5, Switch_connectors.pin7, Switch_connectors.pin9, Switch_connectors.pin11, Arduino_3_3V.VCC, S2.1, S1.1, S3.1, S4.1
  N5: Switch_connectors.pin2, R10.Pin_1, Arduino_3_3V.A3
  N6: Switch_connectors.pin4, R9.Pin_1, Arduino_3_3V.A2
  N7: Switch_connectors.pin6, R8.Pin_1, Arduino_3_3V.A1
  N8: Switch_connectors.pin8, R7.Pin_1, Arduino_3_3V.A0
  N9: Switch_connectors.pin10, R6.Pin_1, Arduino_3_3V.D7
  N10: Switch_connectors.pin12, R5.Pin_1, Arduino_3_3V.D6_PWM
  N11: R1.Pin_1, Arduino_3_3V.D2, S1.2
  N12: R2.Pin_1, Arduino_3_3V.D3_PWM, S2.2
  N13: R3.Pin_1, Arduino_3_3V.D4, S3.2
  N14: R4.Pin_1, Arduino_3_3V.D5_PWM, S4.2
  N15: Arduino_3_3V.D9_PWM, HC_05.pin4
  N16: Arduino_3_3V.D8, HC_05.pin3

notes:
  TSC Handbox V 1.2
  MSpd
  FSel
  FDir
  FStep 1/2/3
  gnd
  pwr
  RX
  TX
  w. Birkfellner 2017
