# Fritzing sketch ConnectorBreakout (saved by Fritzing 0.9.9b)
circuit board: 6.5cm x 5.5cm
breadboards: 1

parts:
  1 = screw terminal, 6 pins
  AA'_BB' = screw terminal, 4 pins
  AA'_BB'_2 = screw terminal, 4 pins
  part = female pin header, 3 pins [form="♀ (female)"]
  part_2 = female pin header, 2 pins [form="♀ (female)"]
  part_3 = female pin header, 2 pins [form="♀ (female)"]
  part_4 = female pin header, 2 pins [form="♀ (female)"]
  part_5 = female pin header, 2 pins [form="♀ (female)"]
  part_6 = female pin header, 3 pins [form="♀ (female)"]
  part_7 = female pin header, 3 pins [form="♀ (female)"]
  part_8 = female pin header, 2 pins [form="♀ (female)"]
  part_9 = female pin header, 2 pins [form="♀ (female)"]
  part_10 = female pin header, 2 pins [form="♀ (female)"]
  part_11 = female pin header, 2 pins [form="♀ (female)"]
  part_12 = female pin header, 3 pins [form="♀ (female)"]
  AA'_BB'1 = screw terminal, 4 pins
  AA'_BB'2 = screw terminal, 4 pins
  1_2 = screw terminal, 6 pins

nets:
  N1: 1.pin1, part.pin1
  N2: 1.pin2, part_6.pin1
  N3: 1.pin3, part.pin2
  N4: 1.pin4, part_6.pin2
  N5: 1.pin5, part.pin3
  N6: 1.pin6, part_6.pin3
  N7: AA'_BB'.pin1, part_2.pin1
  N8: AA'_BB'.pin2, part_3.pin1
  N9: AA'_BB'.pin3, part_2.pin2
  N10: AA'_BB'.pin4, part_3.pin2
  N11: AA'_BB'_2.pin1, part_4.pin1
  N12: AA'_BB'_2.pin2, part_5.pin1
  N13: AA'_BB'_2.pin3, part_4.pin2
  N14: AA'_BB'_2.pin4, part_5.pin2
  N15: part_7.pin1, 1_2.pin2
  N16: part_7.pin2, 1_2.pin4
  N17: part_7.pin3, 1_2.pin6
  N18: part_8.pin1, AA'_BB'1.pin2
  N19: part_8.pin2, AA'_BB'1.pin4
  N20: part_9.pin1, AA'_BB'1.pin1
  N21: part_9.pin2, AA'_BB'1.pin3
  N22: part_10.pin1, AA'_BB'2.pin2
  N23: part_10.pin2, AA'_BB'2.pin4
  N24: part_11.pin1, AA'_BB'2.pin1
  N25: part_11.pin2, AA'_BB'2.pin3
  N26: part_12.pin1, 1_2.pin1
  N27: part_12.pin2, 1_2.pin3
  N28: part_12.pin3, 1_2.pin5

notes:
  ASSMANN WSW A-20041
  ASSMANN WSW A-20040/LP
