# Fritzing sketch MotorBoard (saved by Fritzing 0.9.3b)
circuit board: 6.5cm x 7cm
breadboards: 1

parts:
  C1 = Electrolytic Capacitor [capacitance=1000µF package="300 mil [THT, electrolytic]"]
  Part1 = Arduino Pro Mini v13
  R1 = Resistor [tolerance=±5% resistance=470 package=THT]
  R2 = Resistor [tolerance=±5% resistance=1k package=THT]
  DR_B-EN = female pin header, 8 pins [form="♀ (female)"]
  part = female pin header, 8 pins [form="♀ (female)"]
  part_2 = female pin header, 8 pins [form="♀ (female)"]
  DR_A-EN = female pin header, 8 pins [form="♀ (female)"]
  SPI = female pin header, 5 pins [form="♀ (female)"]
  GND/12V = Screw terminal - 2 pins [package=THT]
  GND/5V = female pin header, 2 pins [form="♀ (female)"]
  DR_B_B2/B1/A2/A1 = female pin header, 4 pins [form="♀ (female)"]
  DR_A_B2/B1/A2/A1 = female pin header, 4 pins [form="♀ (female)"]

nets:
  N1: C1.-, DR_B-EN.pin2, part_2.pin2, GND/12V.pin1
  N2: C1.+, DR_B-EN.pin1, part_2.pin1, GND/12V.pin2
  N3: Part1.GND, DR_B-EN.pin8, part_2.pin8, GND/5V.pin2
  N4: Part1.RAW, DR_B-EN.pin7, part_2.pin7, GND/5V.pin1
  N5: Part1.A1, part.pin1
  N6: Part1.A0, DR_A-EN.pin1
  N7: Part1.D13/SCK, SPI.pin3
  N8: Part1.D12/MISO, R1.Pin_0
  N9: Part1.D11_PWM/MOSI, SPI.pin1
  N10: Part1.D10_PWM/SS, SPI.pin4
  N11: Part1.D8, part.pin2, DR_A-EN.pin2
  N12: Part1.D7, part.pin3, DR_A-EN.pin3
  N13: Part1.D6_PWM, part.pin4, DR_A-EN.pin4
  N14: Part1.D5_PWM, part.pin7
  N15: Part1.D4, part.pin8
  N16: Part1.D3_PWM, DR_A-EN.pin7
  N17: Part1.D2, DR_A-EN.pin8
  N18: R1.Pin_1, R2.Pin_0, SPI.pin2
  N19: R2.Pin_1, SPI.pin5
  N20: DR_B-EN.pin3, DR_B_B2/B1/A2/A1.pin1
  N21: DR_B-EN.pin4, DR_B_B2/B1/A2/A1.pin2
  N22: DR_B-EN.pin5, DR_B_B2/B1/A2/A1.pin3
  N23: DR_B-EN.pin6, DR_B_B2/B1/A2/A1.pin4
  N24: part.pin5, part.pin6
  N25: part_2.pin3, DR_A_B2/B1/A2/A1.pin1
  N26: part_2.pin4, DR_A_B2/B1/A2/A1.pin2
  N27: part_2.pin5, DR_A_B2/B1/A2/A1.pin3
  N28: part_2.pin6, DR_A_B2/B1/A2/A1.pin4
  N29: DR_A-EN.pin5, DR_A-EN.pin6

notes:
  GND/SS/SCK/MISO/MOSI
  TSC
  Motorboard
  W. Birkfellner
  2017-V1.0
  to GND
