# Fritzing sketch TCP_Handbox (saved by Fritzing 0.9.3b)
circuit board: 6.67191cm x 6.98748cm
breadboards: 2

parts:
  Feather_ES32 = Adafruit HUZZAH32 ESP32 Feather [part_number="Adafruit #3405"]
  3_3V/GND/SCL/SDA = screw terminal, 4 pins
  R8 = Resistor [tolerance=±5% resistance=10k package=THT]
  R10 = Resistor [tolerance=±5% resistance=10k package=THT]
  FDir/Foc/Speed = screw terminal, 6 pins
  R5 = Resistor [tolerance=±5% resistance=10k package=THT]
  R6 = Resistor [tolerance=±5% resistance=10k package=THT]
  R7 = Resistor [tolerance=±5% resistance=10k package=THT]
  R4 = Resistor [tolerance=±5% resistance=10k package=THT]
  R3 = Resistor [tolerance=±5% resistance=10k package=THT]
  R2 = Resistor [tolerance=±5% resistance=10k package=THT]
  R1 = Resistor [tolerance=±5% resistance=10k package=THT]
  R9 = Resistor [tolerance=±5% resistance=10k package=THT]
  Full = SWITCH-MOMENTARY-2 [package=tactile-pth]
  F/5 = SWITCH-MOMENTARY-2 [package=tactile-pth]
  F/20 = SWITCH-MOMENTARY-2 [package=tactile-pth]
  N = SWITCH-MOMENTARY-2 [package=tactile-pth-12mm]
  W = SWITCH-MOMENTARY-2 [package=tactile-pth-12mm]
  E = SWITCH-MOMENTARY-2 [package=tactile-pth-12mm]
  S = SWITCH-MOMENTARY-2 [package=tactile-pth-12mm]

nets:
  N1: Feather_ES32.IO21, R5.Pin_1, F/20.2
  N2: Feather_ES32.A5_IO4, R6.Pin_1, F/5.2
  N3: Feather_ES32.A4_IO36, R7.Pin_1, Full.2
  N4: Feather_ES32.A3_I39, R4.Pin_1, W.2
  N5: Feather_ES32.A2_I34, R3.Pin_1, S.2
  N6: Feather_ES32.A1_DAC1, R2.Pin_1, E.2
  N7: Feather_ES32.A0_DAC2, R1.Pin_1, N.2
  N8: Feather_ES32.GND, 3_3V/GND/SCL/SDA.pin2, R8.Pin_0, R10.Pin_0, R5.Pin_0, R6.Pin_0, R7.Pin_0, R4.Pin_0, R3.Pin_0, R2.Pin_0, R1.Pin_0, R9.Pin_0
  N9: Feather_ES32.3.3V, 3_3V/GND/SCL/SDA.pin1, FDir/Foc/Speed.pin2, FDir/Foc/Speed.pin4, FDir/Foc/Speed.pin6, Full.1, F/5.1, F/20.1, N.1, W.1, E.1, S.1
  N10: Feather_ES32.IO27_A10, R10.Pin_1, FDir/Foc/Speed.pin5
  N11: Feather_ES32.IO33_A9, FDir/Foc/Speed.pin3, R9.Pin_1
  N12: Feather_ES32.IO15_A8, R8.Pin_1, FDir/Foc/Speed.pin1
  N13: Feather_ES32.SCL, 3_3V/GND/SCL/SDA.pin3
  N14: Feather_ES32.SDA, 3_3V/GND/SCL/SDA.pin4

notes:
  TSC TCP/IP Handbox
  W. Birkfellner 2018
  I2C OLED
