# Fritzing sketch TSC_Camera_JackV2 (saved by Fritzing 0.9.0b)
circuit board: 8.46667cm x 5.64444cm
breadboards: 1

parts:
  U3 = 2.5mm Audio Jack [package=stereojack2.5mm_stereojack2.5mm]
  Raspberry_Pi_1 = Raspberry Pi 3 [part_number=RPI-3-V1.2]
  R1 = Resistor [tolerance=±5% resistance=4.7k package="0805 [SMD]"]
  IC1 = IC, DIP package, 8 pins [chip_label=ILD74]
  R3 = Resistor [tolerance=±5% resistance=220 package=THT]
  Q1 = NPN-Transistor [part_number=BC547 package="TO92 [THT]"]
  Q2 = NPN-Transistor [part_number=BC547 package="TO92 [THT]"]
  R4 = Resistor [tolerance=±5% resistance=4.7k package="0805 [SMD]"]
  R5 = Resistor [tolerance=±5% resistance=220 package=THT]

nets:
  N1: U3.SLEEVE, IC1.pin5, IC1.pin8
  N2: U3.LEFT, IC1.pin6
  N3: U3.RIGHT, IC1.pin7
  N4: Raspberry_Pi_1.GND, Q1.E, Q2.E
  N5: Raspberry_Pi_1.GIPO16, R1.Pin_0
  N6: Raspberry_Pi_1.GIPO18, R4.Pin_0
  N7: Raspberry_Pi_1.5V, R3.Pin_0, R5.Pin_1
  N8: R1.Pin_1, Q1.B
  N9: IC1.pin1, R3.Pin_1
  N10: IC1.pin2, Q2.C
  N11: IC1.pin3, Q1.C
  N12: IC1.pin4, R5.Pin_0
  N13: Q2.B, R4.Pin_1
