# Fritzing sketch TSC_PiHat_ILD (saved by Fritzing 0.9.3b)
circuit board: 9cm x 7cm
breadboards: 3

parts:
  DS_3231 = Adafruit DS3231 [part_number="Adafruit #3013"]
  ST_4 = RJ12
  FTDI = Adafruit FTDI Friend [part_number="Adafruit #284"]
  R3 = Resistor [tolerance=±5% resistance=4.7k package=THT]
  R4 = Resistor [tolerance=±5% resistance=4.7k package=THT]
  BC547 = TRANSISTOR_NPN [package=to-92-ammo]
  BC547_2 = TRANSISTOR_NPN [package=to-92-ammo]
  RNG = female pin header, 1 pin [form="♀ (female)"]
  TIP = female pin header, 1 pin [form="♀ (female)"]
  GND = female pin header, 1 pin [form="♀ (female)"]
  J1 = double row female pin header, 40 pins [form="♀ (female)"]
  SPI_Mo/Mi(5V)/Cl/SS0/SS1 = screw terminal, 5 pins
  R1 = Resistor [tolerance=±5% resistance=470 package=THT]
  R2 = Resistor [tolerance=±5% resistance=1k package=THT]
  ILD74 = IC, DIP package, 8 pins [chip_label=IC]
  R5 = Resistor [tolerance=±5% resistance=220 package=THT]
  R6 = Resistor [tolerance=±5% resistance=220 package=THT]
  ILD74_2 = IC, DIP package, 8 pins [chip_label=IC]
  BC547_3 = TRANSISTOR_NPN [package=to-92-ammo]
  R7 = Resistor [tolerance=±5% resistance=150 package=THT]
  R8 = Resistor [tolerance=±5% resistance=150 package=THT]
  R11 = Resistor [tolerance=±5% resistance=380 package=THT]
  R12 = Resistor [tolerance=±5% resistance=380 package=THT]
  BC547_4 = TRANSISTOR_NPN [package=to-92-ammo]
  ILD74_3 = IC, DIP package, 8 pins [chip_label=IC]
  BC547_5 = TRANSISTOR_NPN [package=to-92-ammo]
  BC547_6 = TRANSISTOR_NPN [package=to-92-ammo]
  R9 = Resistor [tolerance=±5% resistance=150 package=THT]
  R10 = Resistor [tolerance=±5% resistance=150 package=THT]
  R14 = Resistor [tolerance=±5% resistance=380 package=THT]
  R13 = Resistor [tolerance=±5% resistance=380 package=THT]
  5V_+/GND = Screw terminal - 2 pins [package=THT]
  D1 = Rectifier Diode [part_number=1N4001 package="300 mil [THT]"]

nets:
  N1: DS_3231.Vin, J1.pin1, R11.Pin_0, R12.Pin_1, R14.Pin_1, R13.Pin_0
  GND: DS_3231.GND, FTDI.GND, BC547.E, BC547_2.E, J1.pin5, R2.Pin_1, ILD74_2.pin5, ILD74_2.pin8, ILD74_3.pin5, ILD74_3.pin8
  N2: DS_3231.SCL, J1.pin3
  N3: DS_3231.SDA, J1.pin2
  N4: ST_4.pin_2, BC547_3.B, BC547_4.B, BC547_5.B, BC547_6.B
  N5: ST_4.pin_3, ST_4.pin_4, ST_4.pin_5, ST_4.pin_6, BC547_3.E, BC547_4.E, BC547_5.E, BC547_6.E, D1.cathode
  N6: FTDI.VCC, J1.pin40, R5.Pin_0, R6.Pin_1
  N7: FTDI.TX, J1.pin36
  N8: FTDI.RX, J1.pin37
  N9: R3.Pin_0, J1.pin23
  N10: R3.Pin_1, BC547.B
  N11: R4.Pin_0, J1.pin35
  N12: R4.Pin_1, BC547_2.B
  N13: BC547.C, ILD74.pin3
  N14: BC547_2.C, ILD74.pin2
  N15: RNG.pin1, ILD74.pin6
  N16: TIP.pin1, ILD74.pin7
  N17: GND.pin1, ILD74.pin5, ILD74.pin8
  N18: J1.pin7, ILD74_3.pin7, R13.Pin_1
  N19: J1.pin8, ILD74_2.pin7, R11.Pin_1
  N20: J1.pin10, SPI_Mo/Mi(5V)/Cl/SS0/SS1.pin1
  N21: J1.pin11, R1.Pin_1, R2.Pin_0
  N22: J1.pin12, SPI_Mo/Mi(5V)/Cl/SS0/SS1.pin3
  N23: J1.pin28, SPI_Mo/Mi(5V)/Cl/SS0/SS1.pin5
  N24: J1.pin29, SPI_Mo/Mi(5V)/Cl/SS0/SS1.pin4
  N25: J1.pin32, ILD74_2.pin6, R12.Pin_0
  N26: J1.pin33, ILD74_3.pin6, R14.Pin_0
  N27: SPI_Mo/Mi(5V)/Cl/SS0/SS1.pin2, R1.Pin_0
  N28: ILD74.pin1, R5.Pin_1
  N29: ILD74.pin4, R6.Pin_0
  N30: ILD74_2.pin1, BC547_3.C
  N31: ILD74_2.pin2, R7.Pin_1
  N32: ILD74_2.pin3, R8.Pin_0
  N33: ILD74_2.pin4, BC547_4.C
  N34: R7.Pin_0, R8.Pin_1, R9.Pin_0, R10.Pin_1, 5V_+/GND.pin2
  N35: ILD74_3.pin1, BC547_5.C
  N36: ILD74_3.pin2, R9.Pin_1
  N37: ILD74_3.pin4, BC547_6.C, R10.Pin_0
  N38: 5V_+/GND.pin1, D1.anode

notes:
  TSC  V1.2
  Vin
  GND
  DSLR
  W. Birkfellner/S. Elste 2017

custom parts:
  Adafruit DS3231: The datasheet for the DS3231 explains that this part is an "Extremely Accurate I²C-Integrated RTC/TCXO/Crystal". And, hey, it does exactly what it says on the tin! This Real Time Clock (RTC) is the most precise you can get in a small, low power package. Most RTCs use an external 32kHz timing crystal that is used to keep time with low current draw. And that's all well and good, but those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
  Adafruit FTDI Friend: Long gone are the days of parallel ports and serial ports. Now the USB port reigns supreme! But USB is hard, and you just want to transfer your every-day serial data from a microcontroller to computer. What now? Enter the FTDI Friend! The FTDI Friend is a tweaked out FTDI FT232RL chip adapter. Sure, like the well-known FTDI cable, it can provide power to your project and there are 4 signal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
