# Fritzing sketch TSC_PiHat_ILD (saved by Fritzing 0.9.3b)
circuit board: 9cm x 7cm
breadboards: 3

parts:
  DS_3231 = Adafruit DS3231 [part_number="Adafruit #3013"]
  ST_4 = RJ12
  FTDI = Adafruit FTDI Friend [part_number="Adafruit #284"]
  R2 = Resistor [tolerance=±5% resistance=4.7k package=THT]
  R3 = Resistor [tolerance=±5% resistance=4.7k package=THT]
  BC547 = TRANSISTOR_NPN [package=to-92-ammo]
  BC547_2 = TRANSISTOR_NPN [package=to-92-ammo]
  RNG = female pin header, 1 pin [form="♀ (female)"]
  TIP = female pin header, 1 pin [form="♀ (female)"]
  GND = female pin header, 1 pin [form="♀ (female)"]
  J1 = double row female pin header, 40 pins [form="♀ (female)"]
  SPI_Mo/Mi/Cl/SS0/SS1 = screw terminal, 5 pins
  R4 = Resistor [tolerance=±5% resistance=470 package=THT]
  R5 = Resistor [tolerance=±5% resistance=1k package=THT]
  ILD74 = IC, DIP package, 8 pins [chip_label=IC]
  R10 = Resistor [tolerance=±5% resistance=220 package=THT]
  R11 = Resistor [tolerance=±5% resistance=220 package=THT]
  ILD74_2 = IC, DIP package, 8 pins [chip_label=IC]
  BC547_3 = TRANSISTOR_NPN [package=to-92-ammo]
  R12 = Resistor [tolerance=±5% resistance=880 package=THT]
  R13 = Resistor [tolerance=±5% resistance=880 package=THT]
  R14 = Resistor [tolerance=±5% resistance=8.3M package=THT]
  R15 = Resistor [tolerance=±5% resistance=5.1k package=THT]
  R17 = Resistor [tolerance=±5% resistance=8.3M package=THT]
  R18 = Resistor [tolerance=±5% resistance=5.1k package=THT]
  BC547_4 = TRANSISTOR_NPN [package=to-92-ammo]
  ILD74_3 = IC, DIP package, 8 pins [chip_label=IC]
  BC547_5 = TRANSISTOR_NPN [package=to-92-ammo]
  BC547_6 = TRANSISTOR_NPN [package=to-92-ammo]
  R19 = Resistor [tolerance=±5% resistance=880 package=THT]
  R20 = Resistor [tolerance=±5% resistance=880 package=THT]
  R21 = Resistor [tolerance=±5% resistance=8.3M package=THT]
  R22 = Resistor [tolerance=±5% resistance=8.3M package=THT]
  R23 = Resistor [tolerance=±5% resistance=5.1k package=THT]
  R24 = Resistor [tolerance=±5% resistance=5.1k package=THT]

nets:
  N1: DS_3231.Vin, ST_4.pin_3, ST_4.pin_4, ST_4.pin_5, ST_4.pin_6, J1.pin1, ILD74_2.pin5, ILD74_2.pin8, R12.Pin_0, R13.Pin_1, R15.Pin_1, R18.Pin_0, BC547_4.E, ILD74_3.pin5, ILD74_3.pin8, R19.Pin_0, R20.Pin_1, R23.Pin_0, R24.Pin_1
  GND: DS_3231.GND, FTDI.GND, BC547.E, BC547_2.E, J1.pin5, R5.Pin_1, BC547_3.E, R14.Pin_0, R15.Pin_0, R18.Pin_1, BC547_5.E, BC547_6.E, R22.Pin_0, R23.Pin_1, R24.Pin_0
  N2: DS_3231.SCL, J1.pin3
  N3: DS_3231.SDA, J1.pin2
  N4: ST_4.pin_2, BC547_3.B, BC547_4.B, BC547_5.B, BC547_6.B
  N5: FTDI.VCC, J1.pin40, R10.Pin_0, R11.Pin_1
  N6: FTDI.TX, J1.pin36
  N7: FTDI.RX, J1.pin37
  N8: R2.Pin_0, J1.pin23
  N9: R2.Pin_1, BC547.B
  N10: R3.Pin_0, J1.pin35
  N11: R3.Pin_1, BC547_2.B
  N12: BC547.C, ILD74.pin3
  N13: BC547_2.C, ILD74.pin2
  N14: RNG.pin1, ILD74.pin6
  N15: TIP.pin1, ILD74.pin7
  N16: GND.pin1, ILD74.pin5, ILD74.pin8
  N17: J1.pin7, ILD74_3.pin7, R22.Pin_1
  N18: J1.pin8, ILD74_2.pin7, R14.Pin_1
  N19: J1.pin10, SPI_Mo/Mi/Cl/SS0/SS1.pin1
  N20: J1.pin11, R4.Pin_1, R5.Pin_0
  N21: J1.pin12, SPI_Mo/Mi/Cl/SS0/SS1.pin3
  N22: J1.pin28, SPI_Mo/Mi/Cl/SS0/SS1.pin5
  N23: J1.pin29, SPI_Mo/Mi/Cl/SS0/SS1.pin4
  N24: J1.pin32, ILD74_2.pin6, R17.Pin_0
  N25: J1.pin33, ILD74_3.pin6, R21.Pin_0
  N26: J1.pin38, R17.Pin_1, R21.Pin_1
  N27: SPI_Mo/Mi/Cl/SS0/SS1.pin2, R4.Pin_0
  N28: ILD74.pin1, R10.Pin_1
  N29: ILD74.pin4, R11.Pin_0
  N30: ILD74_2.pin1, R12.Pin_1
  N31: ILD74_2.pin2, BC547_3.C
  N32: ILD74_2.pin3, BC547_4.C
  N33: ILD74_2.pin4, R13.Pin_0
  N34: ILD74_3.pin1, R19.Pin_1
  N35: ILD74_3.pin2, BC547_5.C
  N36: ILD74_3.pin3, BC547_6.C
  N37: ILD74_3.pin4, R20.Pin_0

notes:
  TSC  V1.2
  Vin
  GND
  DSLR
  W. Birkfellner/S. Elste 2017

custom parts:
  Adafruit DS3231: The datasheet for the DS3231 explains that this part is an "Extremely Accurate I²C-Integrated RTC/TCXO/Crystal". And, hey, it does exactly what it says on the tin! This Real Time Clock (RTC) is the most precise you can get in a small, low power package. Most RTCs use an external 32kHz timing crystal that is used to keep time with low current draw. And that's all well and good, but those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
  Adafruit FTDI Friend: Long gone are the days of parallel ports and serial ports. Now the USB port reigns supreme! But USB is hard, and you just want to transfer your every-day serial data from a microcontroller to computer. What now? Enter the FTDI Friend! The FTDI Friend is a tweaked out FTDI FT232RL chip adapter. Sure, like the well-known FTDI cable, it can provide power to your project and there are 4 signal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
