# Fritzing sketch Bigger4DriveBoard (saved by Fritzing 0.9.3b)
circuit board: 9cm x 8cm
breadboards: 3

parts:
  SPI_MO/SC/CS/MI = screw terminal, 4 pins
  5V_GND/+ = Screw terminal - 2 pins [package=THT]
  Aux_1_VMot = Pololu A4988 [package=SO16]
  Aux_2_VMot = Pololu A4988 [package=SO16]
  DRV_1_Dir = DRV 8825 Stepper Motor Carrier, High Current [part_number="DRV 8825"]
  DRV_2_Dir = DRV 8825 Stepper Motor Carrier, High Current [part_number="DRV 8825"]
  Drive_2 = screw terminal, 4 pins
  Aux_Drive_2 = screw terminal, 4 pins
  Aux_Drive_1 = screw terminal, 4 pins
  12V_GND/+ = Screw terminal - 2 pins [package=THT]
  Teensy_GND = female pin header, 24 pins [form="♀ (female)"]
  Teensy_5_V = female pin header, 24 pins [form="♀ (female)"]
  C1 = Electrolytic Capacitor [capacitance=4.7mF voltage=0.1kV package="200 mil [THT, electrolytic]"]
  Drive_1 = screw terminal, 4 pins

nets:
  N1: SPI_MO/SC/CS/MI.pin1, Teensy_GND.pin13
  N2: SPI_MO/SC/CS/MI.pin2, Teensy_5_V.pin11
  N3: SPI_MO/SC/CS/MI.pin3, Teensy_GND.pin11
  N4: SPI_MO/SC/CS/MI.pin4, Teensy_GND.pin12
  N5: 5V_GND/+.pin1, Teensy_5_V.pin24
  N6: 5V_GND/+.pin2, Aux_1_VMot.GND#8, Aux_2_VMot.GND#8, DRV_1_Dir.GROUND_LOG, DRV_2_Dir.GROUND_LOG, Teensy_GND.pin24
  N7: Aux_1_VMot.ENABLE, Teensy_5_V.pin14
  N8: Aux_1_VMot.MS1, Aux_2_VMot.MS1, Teensy_5_V.pin20
  N9: Aux_1_VMot.MS2, Aux_2_VMot.MS2, Teensy_5_V.pin19
  N10: Aux_1_VMot.MS3, Aux_2_VMot.MS3, Teensy_5_V.pin18
  N11: Aux_1_VMot.RESET, Aux_1_VMot.SLEEP
  N12: Aux_1_VMot.STEP, Teensy_5_V.pin8
  N13: Aux_1_VMot.DIR, Teensy_5_V.pin4
  VDD: Aux_1_VMot.VDD, Aux_2_VMot.VDD, DRV_1_Dir.VOLTAGE_DD, DRV_2_Dir.VOLTAGE_DD, Teensy_GND.pin10
  N14: Aux_1_VMot.1B, Aux_Drive_1.pin4
  N15: Aux_1_VMot.1A, Aux_Drive_1.pin3
  N16: Aux_1_VMot.2A, Aux_Drive_1.pin2
  N17: Aux_1_VMot.2B, Aux_Drive_1.pin1
  N18: Aux_1_VMot.GND#14, Aux_2_VMot.GND#14, DRV_1_Dir.GROUND_ST/_MT, DRV_2_Dir.GROUND_ST/_MT, 12V_GND/+.pin2, C1.-
  N19: Aux_1_VMot.VMOT, Aux_2_VMot.VMOT, DRV_1_Dir.VOLTAGE_ST/_MT, DRV_2_Dir.VOLTAGE_ST/_MT, 12V_GND/+.pin1, C1.+
  N20: Aux_2_VMot.ENABLE, Teensy_5_V.pin13
  N21: Aux_2_VMot.RESET, Aux_2_VMot.SLEEP
  N22: Aux_2_VMot.STEP, Teensy_5_V.pin7
  N23: Aux_2_VMot.DIR, Teensy_5_V.pin3
  N24: Aux_2_VMot.1B, Aux_Drive_2.pin4
  N25: Aux_2_VMot.1A, Aux_Drive_2.pin3
  N26: Aux_2_VMot.2A, Aux_Drive_2.pin2
  N27: Aux_2_VMot.2B, Aux_Drive_2.pin1
  N28: DRV_1_Dir.ENABLE, Teensy_5_V.pin9
  N29: DRV_1_Dir.MS1, DRV_2_Dir.MS1, Teensy_5_V.pin17
  N30: DRV_1_Dir.MS2, DRV_2_Dir.MS2, Teensy_5_V.pin16
  N31: DRV_1_Dir.MS3, DRV_2_Dir.MS3, Teensy_5_V.pin15
  N32: DRV_1_Dir.RESET, DRV_1_Dir.SLEEP
  N33: DRV_1_Dir.STEP, Teensy_5_V.pin5
  N34: DRV_1_Dir.DIRECTION, Teensy_5_V.pin1
  N35: DRV_1_Dir.OUT_2B, Drive_2.pin1
  N36: DRV_1_Dir.OUT_2A, Drive_2.pin2
  N37: DRV_1_Dir.OUT_1A, Drive_2.pin3
  N38: DRV_1_Dir.OUT_1B, Drive_2.pin4
  N39: DRV_2_Dir.ENABLE, Teensy_5_V.pin12
  N40: DRV_2_Dir.RESET, DRV_2_Dir.SLEEP
  N41: DRV_2_Dir.STEP, Teensy_5_V.pin6
  N42: DRV_2_Dir.DIRECTION, Teensy_5_V.pin2
  N43: DRV_2_Dir.OUT_2B, Drive_1.pin1
  N44: DRV_2_Dir.OUT_2A, Drive_1.pin2
  N45: DRV_2_Dir.OUT_1A, Drive_1.pin3
  N46: DRV_2_Dir.OUT_1B, Drive_1.pin4
