# Fritzing sketch TSC_PiHat (saved by Fritzing 0.9.0b)
circuit board: 10.2521cm x 8.16731cm
breadboards: 2

parts:
  DS_3241 = Adafruit DS3231 [part_number="Adafruit #3013"]
  IC1 = IC, DIP package, 16 pins [chip_label=IC]
  J2 = female pin header, 6 pins [form="♀ (female)"]
  U1 = DIODE-ZENER [package=diode-zener]
  ST_4 = RJ12
  Pi = double row female pin header, 40 pins [form="♀ (female)"]
  R1 = Resistor [tolerance=±5% resistance=100 package=THT]
  PWR_out_(GND/3_3/5) = screw terminal, 3 pins
  FTDI = Adafruit FTDI Friend [part_number="Adafruit #284"]
  R2 = Resistor [tolerance=±5% resistance=4.7k package=THT]
  R3 = Resistor [tolerance=±5% resistance=4.7k package=THT]
  BC547 = TRANSISTOR_NPN [package=to-92-ammo]
  BC547_2 = TRANSISTOR_NPN [package=to-92-ammo]
  J3 = female pin header, 1 pin [form="♀ (female)"]
  J4 = female pin header, 1 pin [form="♀ (female)"]
  J5 = female pin header, 1 pin [form="♀ (female)"]
  GPIO = female pin header, 6 pins [form="♀ (female)"]
  SPI_Mo/Mi/Cl/GND = screw terminal, 6 pins

nets:
  VIN: DS_3241.Vin, Pi.pin1, FTDI.VCC
  GND: DS_3241.GND, IC1.pin2, IC1.pin8, J2.pin2, ST_4.pin_2, Pi.pin5, PWR_out_(GND/3_3/5).pin3, FTDI.GND, BC547.E, BC547_2.E, J5.pin1
  N1: DS_3241.SCL, Pi.pin3
  N2: DS_3241.SDA, Pi.pin2
  N3: IC1.pin1, J2.pin1, Pi.pin40, PWR_out_(GND/3_3/5).pin2
  N4: IC1.pin3, ST_4.pin_5
  N5: IC1.pin4, ST_4.pin_4
  N6: IC1.pin5, ST_4.pin_3
  N7: IC1.pin6, ST_4.pin_6
  N8: IC1.pin9, IC1.pin15, J2.pin4, U1.A
  N9: IC1.pin11, Pi.pin8
  N10: IC1.pin12, Pi.pin32
  N11: IC1.pin13, Pi.pin33
  N12: IC1.pin14, Pi.pin7
  N13: IC1.pin16, U1.C, R1.Pin_0
  N14: J2.pin6, R1.Pin_1
  N15: Pi.pin9, PWR_out_(GND/3_3/5).pin1
  N16: Pi.pin10, SPI_Mo/Mi/Cl/GND.pin1
  N17: Pi.pin11, SPI_Mo/Mi/Cl/GND.pin2
  N18: Pi.pin12, SPI_Mo/Mi/Cl/GND.pin3
  N19: Pi.pin13, SPI_Mo/Mi/Cl/GND.pin4
  N20: Pi.pin15, GPIO.pin1
  N21: Pi.pin16, GPIO.pin2
  N22: Pi.pin17, GPIO.pin3
  N23: Pi.pin18, GPIO.pin4
  N24: Pi.pin19, GPIO.pin5
  N25: Pi.pin20, GPIO.pin6
  N26: Pi.pin23, R2.Pin_0
  N27: Pi.pin28, SPI_Mo/Mi/Cl/GND.pin6
  N28: Pi.pin29, SPI_Mo/Mi/Cl/GND.pin5
  N29: Pi.pin35, R3.Pin_0
  N30: Pi.pin36, FTDI.TX
  N31: Pi.pin37, FTDI.RX
  N32: R2.Pin_1, BC547.B
  N33: R3.Pin_1, BC547_2.B
  N34: BC547.C, J3.pin1
  N35: BC547_2.C, J4.pin1

notes:
  TSC
  V. 1
  W. Birkfellner  2017

custom parts:
  Adafruit DS3231: The datasheet for the DS3231 explains that this part is an "Extremely Accurate I²C-Integrated RTC/TCXO/Crystal". And, hey, it does exactly what it says on the tin! This Real Time Clock (RTC) is the most precise you can get in a small, low power package. Most RTCs use an external 32kHz timing crystal that is used to keep time with low current draw. And that's all well and good, but those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
  Adafruit FTDI Friend: Long gone are the days of parallel ports and serial ports. Now the USB port reigns supreme! But USB is hard, and you just want to transfer your every-day serial data from a microcontroller to computer. What now? Enter the FTDI Friend! The FTDI Friend is a tweaked out FTDI FT232RL chip adapter. Sure, like the well-known FTDI cable, it can provide power to your project and there are 4 signal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
