# Fritzing sketch TSC_PiHat_SMD_ADuM (saved by Fritzing 0.9.3b)
circuit board: 9.96696cm x 8.16287cm
breadboards: 2

parts:
  DS_3231 = Adafruit DS3231 [part_number="Adafruit #3013"]
  ST_4 = RJ12
  FTDI = Adafruit FTDI Friend [part_number="Adafruit #284"]
  R2 = Resistor [tolerance=±5% resistance=4.7k package=THT]
  R3 = Resistor [tolerance=±5% resistance=4.7k package=THT]
  BC547 = TRANSISTOR_NPN [package=to-92-ammo]
  BC547_2 = TRANSISTOR_NPN [package=to-92-ammo]
  RNG = female pin header, 1 pin [form="♀ (female)"]
  TIP = female pin header, 1 pin [form="♀ (female)"]
  GND = female pin header, 1 pin [form="♀ (female)"]
  GPIO = female pin header, 6 pins [form="♀ (female)"]
  SPI_Mo/Mi/Cl/GND = screw terminal, 6 pins
  D1 = Zener Diode [part_number=1N4732A breakdown_voltage=3.6V package="300 mil [THT]"]
  R4 = Resistor [tolerance=±5% resistance=380 package=THT]
  D2 = Zener Diode [part_number=1N4732A breakdown_voltage=3.6V package="300 mil [THT]"]
  R5 = Resistor [tolerance=±5% resistance=380 package=THT]
  D3 = Zener Diode [part_number=1N4732A breakdown_voltage=3.6V package="300 mil [THT]"]
  R6 = Resistor [tolerance=±5% resistance=380 package=THT]
  R7 = Resistor [tolerance=±5% resistance=380 package=THT]
  ADuM = SOIC18-W [chip_label=SOIC18-W package=SO(w)]
  D4 = Zener Diode [part_number=1N4732A breakdown_voltage=3.6V package="300 mil [THT]"]
  PWR = female pin header, 3 pins [form="♀ (female)"]
  J2 = double row female pin header, 40 pins [form="♀ (female)"]

nets:
  N1: DS_3231.Vin, PWR.pin1, J2.pin1
  GND: DS_3231.GND, ST_4.pin_2, FTDI.GND, BC547.E, BC547_2.E, GND.pin1, D1.anode, D2.anode, D3.anode, ADuM.2, ADuM.8, ADuM.11, ADuM.17, D4.anode, J2.pin5
  N2: DS_3231.SCL, J2.pin3
  N3: DS_3231.SDA, J2.pin2
  N4: ST_4.pin_3, ADuM.3
  N5: ST_4.pin_4, ADuM.4
  N6: ST_4.pin_5, ADuM.5
  N7: ST_4.pin_6, ADuM.6
  N8: FTDI.VCC, ADuM.1, ADuM.18, PWR.pin2, J2.pin40
  N9: FTDI.TX, J2.pin36
  N10: FTDI.RX, J2.pin37
  N11: R2.Pin_0, J2.pin23
  N12: R2.Pin_1, BC547.B
  N13: R3.Pin_0, J2.pin35
  N14: R3.Pin_1, BC547_2.B
  N15: BC547.C, RNG.pin1
  N16: BC547_2.C, TIP.pin1
  N17: GPIO.pin1, J2.pin15
  N18: GPIO.pin2, J2.pin16
  N19: GPIO.pin3, J2.pin17
  N20: GPIO.pin4, J2.pin18
  N21: GPIO.pin5, J2.pin19
  N22: GPIO.pin6, J2.pin20
  N23: SPI_Mo/Mi/Cl/GND.pin1, J2.pin10
  N24: SPI_Mo/Mi/Cl/GND.pin2, J2.pin11
  N25: SPI_Mo/Mi/Cl/GND.pin3, J2.pin12
  N26: SPI_Mo/Mi/Cl/GND.pin4, J2.pin13
  N27: SPI_Mo/Mi/Cl/GND.pin5, J2.pin29
  N28: SPI_Mo/Mi/Cl/GND.pin6, J2.pin28
  N29: D1.cathode, R4.Pin_0, J2.pin7
  N30: R4.Pin_1, ADuM.16
  N31: D2.cathode, R5.Pin_0, J2.pin33
  N32: R5.Pin_1, ADuM.15
  N33: D3.cathode, R6.Pin_0, J2.pin32
  N34: R6.Pin_1, ADuM.14
  N35: R7.Pin_0, D4.cathode, J2.pin8
  N36: R7.Pin_1, ADuM.13
  N37: PWR.pin3, J2.pin6

notes:
  TSC
  V. 1
  Vin
  GND
  DSLR
  W. Birkfellner  2017

custom parts:
  Adafruit DS3231: The datasheet for the DS3231 explains that this part is an "Extremely Accurate I²C-Integrated RTC/TCXO/Crystal". And, hey, it does exactly what it says on the tin! This Real Time Clock (RTC) is the most precise you can get in a small, low power package. Most RTCs use an external 32kHz timing crystal that is used to keep time with low current draw. And that's all well and good, but those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
  Adafruit FTDI Friend: Long gone are the days of parallel ports and serial ports. Now the USB port reigns supreme! But USB is hard, and you just want to transfer your every-day serial data from a microcontroller to computer. What now? Enter the FTDI Friend! The FTDI Friend is a tweaked out FTDI FT232RL chip adapter. Sure, like the well-known FTDI cable, it can provide power to your project and there are 4 signal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
